# Fritzing sketch connection (saved by Fritzing 0.8.7b)
breadboards: 1

parts:
  U1 = Spark Core (v1.0)
  U2 = RF-LINK_TX [package=rf-link_tx]

nets:
  3V3: U1.A2, U1.3V3, U2.+5V
  N1: U1.A3, U1.A6
  N2: U1.A5, U1.VIN
  GND: U1.GND, U2.GND
  N3: U1.D0, U2.DATA

notes:
  ANT

custom parts:
  Spark Core (v1.0): The Spark Core is a tiny Wi-Fi development board that makes it easy to create internet-connected hardware. The Core is all you need to get started; power it over USB and in minutes you'll be controlling LEDs, switches and motors and collecting data from sensors over the internet! It has 8 digital I/O pins, 8 analog I/O pins, 8 PWM pins; UART (Serial), SPI, I2C, and JTAG peripherals available.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
